// Logisim project pg09_abus_sel.circ as structural Verilog: 1 circuit, main circuit main
module main (
  input  in_1,
  input  in_2,
  input  in_3,
  input  in_4,
  input  in_5,
  input  in_6,
  input  in_7
);

  wire aCPU, aINTC, and_3_out, and_4_out, and_5_out, and_6_out, and_11_out, and_12_out, and_13_out,
       and_14_out, and_15_out, and_16_out, and_17_out, and_18_out, and_19_out, and_20_out, and_21_out,
       and_22_out, and_25_out, and_27_out, and_29_out, and_31_out, and_33_out, and_34_out, FIRQ, HALTACK,
       INTACK, IRQ, nA1, nA2, nA3, nBA, nBS, nIVV, NMI, NORMAL, nRWB, or_1_out, or_2_out, or_3_out, or_4_out,
       or_5_out, or_6_out, or_7_out, or_8_out, RESERVED, RESET, SWI, SWI2, SWI3, SYNCACK;

  not not_1 (nBA, in_1);
  not not_2 (nBS, in_2);
  and and_1 (NORMAL, nBA, nBS);
  and and_2 (SYNCACK, in_1, nBS);
  and and_3 (and_3_out, nA3, nA2);
  and and_4 (and_4_out, nA3, in_6);
  and and_5 (and_5_out, in_5, nA2);
  and and_6 (and_6_out, in_5, in_6);
  not not_3 (nA1, in_7);
  not not_4 (nA2, in_6);
  and and_7 (RESERVED, and_3_out, nA1);
  and and_8 (SWI2, and_4_out, nA1);
  and and_9 (IRQ, and_5_out, nA1);
  and and_10 (NMI, and_6_out, nA1);
  or or_1 (or_1_out, NORMAL, and_11_out);
  and and_11 (and_11_out, INTACK, RESERVED);
  and and_12 (and_12_out, INTACK, SWI3);
  or or_2 (or_2_out, and_12_out, and_13_out);
  and and_13 (and_13_out, INTACK, SWI2);
  and and_14 (and_14_out, INTACK, FIRQ);
  or or_3 (or_3_out, and_14_out, and_15_out);
  and and_15 (and_15_out, INTACK, SWI);
  and and_16 (and_16_out, INTACK, NMI);
  or or_4 (or_4_out, and_16_out, and_17_out);
  and and_17 (and_17_out, INTACK, RESET);
  and and_18 (and_18_out, INTACK, IRQ);
  and and_19 (and_19_out, and_18_out, nRWB);
  and and_20 (and_20_out, INTACK, IRQ);
  and and_21 (and_21_out, and_20_out, and_22_out);
  and and_22 (and_22_out, in_3, nIVV);
  or or_5 (or_5_out, or_1_out, or_2_out);
  or or_6 (or_6_out, or_3_out, or_4_out);
  or or_7 (or_7_out, and_19_out, and_21_out);
  LED led_1 (.in(aCPU));
  LED led_2 (.in(aINTC));
  not not_5 (nA3, in_5);
  and and_23 (INTACK, nBA, in_2);
  and and_24 (HALTACK, in_1, in_2);
  or or_8 (or_8_out, or_5_out, or_6_out);
  and and_25 (and_25_out, nA3, nA2);
  and and_26 (SWI3, and_25_out, in_7);
  and and_27 (and_27_out, nA3, in_6);
  and and_28 (FIRQ, and_27_out, in_7);
  and and_29 (and_29_out, in_5, nA2);
  and and_30 (SWI, and_29_out, in_7);
  and and_31 (and_31_out, in_5, in_6);
  and and_32 (RESET, and_31_out, in_7);
  or or_9 (aCPU, or_8_out, or_7_out);
  and and_33 (and_33_out, INTACK, IRQ);
  and and_34 (and_34_out, in_3, in_4);
  not not_6 (nIVV, in_4);
  not not_7 (nRWB, in_3);
  and and_35 (aINTC, and_33_out, and_34_out);

  // Other names for the same wires on the sheet: A1 = in_7; A2 = in_6; A3 = in_5; BA = in_1; BS = in_2; IVV = in_4;
  //   RWB = in_3

  // Notes on the sheet:
  //   Inverted copies of input signals.
  //   Decode A1-A3 into vector.
  //   CPU states based on BA and BS outputs from 6809.
  //   CPU drives address bus when INTC does not.
  //   (Fully-enumerated, because that's how it's implemented in the GAL.)
  //   These outputs are active-low in hardware, but shown active-high here for illustration purposes.
  //   INTC drives address bus when INTACK & IRQ & read & Vector Valid (from INTMUXAV)
endmodule
