// Logisim project pg09_addr_decode_io_option1.circ as structural Verilog: 1 circuit, main circuit main
module main (
  input  in_1,
  input  in_2,
  input  in_3,
  input  in_4,
  input  in_5,
  input  in_6,
  input  in_7,
  input  in_8,
  input  in_9,
  input  in_10,
  input  in_11
);

  wire nIO0SEL, nIO1SEL, nIO2SEL, nIO3SEL, nIO4SEL, nIO5SEL, nIO6SEL, nIO7SEL, nIO8SEL, nIO9SEL, nIO10SEL,
       nIO11SEL, nIO12SEL, nIO13SEL, nIO14SEL, nIO15SEL, nIO16SEL, nIO17SEL, nIO18SEL, nIO19SEL, nIO20SEL,
       nIO21SEL, nIO22SEL, nIO23SEL, nIO24SEL, nIO25SEL, nIO26SEL, nIO27SEL, nIO28SEL, nIO29SEL, nIO30SEL,
       nIO31SEL, not_1_out, not_2_out;

  not not_1 (not_1_out, in_9);
  not not_2 (not_2_out, in_10);
  _74138 u_74138_1 (
    .pin1(in_6), .pin2(in_7), .pin3(in_8), .pin4(in_11), .pin5(in_9), .pin6(not_2_out), .pin7(nIO7SEL),
    .pin15(nIO0SEL), .pin14(nIO1SEL), .pin13(nIO2SEL), .pin12(nIO3SEL), .pin11(nIO4SEL), .pin10(nIO5SEL),
    .pin9(nIO6SEL));
  _74138 u_74138_2 (
    .pin1(in_6), .pin2(in_7), .pin3(in_8), .pin4(in_11), .pin5(not_1_out), .pin6(not_2_out), .pin7(nIO15SEL),
    .pin15(nIO8SEL), .pin14(nIO9SEL), .pin13(nIO10SEL), .pin12(nIO11SEL), .pin11(nIO12SEL), .pin10(nIO13SEL),
    .pin9(nIO14SEL));
  _74138 u_74138_3 (
    .pin1(in_6), .pin2(in_7), .pin3(in_8), .pin4(in_11), .pin5(in_9), .pin6(in_10), .pin7(nIO23SEL),
    .pin15(nIO16SEL), .pin14(nIO17SEL), .pin13(nIO18SEL), .pin12(nIO19SEL), .pin11(nIO20SEL),
    .pin10(nIO21SEL), .pin9(nIO22SEL));
  _74138 u_74138_4 (
    .pin1(in_6), .pin2(in_7), .pin3(in_8), .pin4(in_11), .pin5(not_1_out), .pin6(in_10), .pin7(nIO31SEL),
    .pin15(nIO24SEL), .pin14(nIO25SEL), .pin13(nIO26SEL), .pin12(nIO27SEL), .pin11(nIO28SEL),
    .pin10(nIO29SEL), .pin9(nIO30SEL));

  // Other names for the same wires on the sheet: A0 = in_1; A1 = in_2; A2 = in_3; A3 = in_4; A4 = in_5; A5 = in_6;
  //   A6 = in_7; A7 = in_8; A8 = in_9; A9 = in_10; nIOSEL = in_11

  // Notes on the sheet:
  //   Typical propagation delay: 34ns (1st decoder - IOSEL) + 13ns (inverter) + 34ns (2nd decoder) = 81ns
endmodule
