// Logisim project pg09_addr_decode_io_option2.circ as structural Verilog: 1 circuit, main circuit main
module main (
  input  in_1,
  input  in_2,
  input  in_3,
  input  in_4,
  input  in_5,
  input  in_6,
  input  in_7,
  input  in_8,
  input  in_9,
  input  in_10,
  input  in_11
);

  wire n74138_1_pin4, n74138_2_pin4, n74138_3_pin4, n74138_4_pin4, nIO0, nIO0SEL, nIO1, nIO1SEL, nIO2,
       nIO2SEL, nIO3, nIO3SEL, nIO4, nIO4SEL, nIO5, nIO5SEL, nIO6, nIO6SEL, nIO7, nIO7SEL, nIO8, nIO8SEL,
       nIO9, nIO9SEL, nIO10, nIO10SEL, nIO11, nIO11SEL, nIO12, nIO12SEL, nIO13, nIO13SEL, nIO14, nIO14SEL,
       nIO15, nIO15SEL, nIO16, nIO16SEL, nIO17, nIO17SEL, nIO18, nIO18SEL, nIO19, nIO19SEL, nIO20, nIO20SEL,
       nIO21, nIO21SEL, nIO22, nIO22SEL, nIO23, nIO23SEL, nIO24, nIO24SEL, nIO25, nIO25SEL, nIO26, nIO26SEL,
       nIO27, nIO27SEL, nIO28, nIO28SEL, nIO29, nIO29SEL, nIO30, nIO30SEL, nIO31, nIO31SEL, not_1_out,
       not_2_out;

  not not_1 (not_1_out, in_9);
  not not_2 (not_2_out, in_10);
  _74138 u_74138_1 (
    .pin1(in_6), .pin2(in_7), .pin3(in_8), .pin4(n74138_1_pin4), .pin5(in_9), .pin6(not_2_out), .pin7(nIO7),
    .pin15(nIO0), .pin14(nIO1), .pin13(nIO2), .pin12(nIO3), .pin11(nIO4), .pin10(nIO5), .pin9(nIO6));
  _74138 u_74138_2 (
    .pin1(in_6), .pin2(in_7), .pin3(in_8), .pin4(n74138_2_pin4), .pin5(not_1_out), .pin6(not_2_out),
    .pin7(nIO15), .pin15(nIO8), .pin14(nIO9), .pin13(nIO10), .pin12(nIO11), .pin11(nIO12), .pin10(nIO13),
    .pin9(nIO14));
  _74138 u_74138_3 (
    .pin1(in_6), .pin2(in_7), .pin3(in_8), .pin4(n74138_3_pin4), .pin5(in_9), .pin6(in_10), .pin7(nIO23),
    .pin15(nIO16), .pin14(nIO17), .pin13(nIO18), .pin12(nIO19), .pin11(nIO20), .pin10(nIO21), .pin9(nIO22));
  _74138 u_74138_4 (
    .pin1(in_6), .pin2(in_7), .pin3(in_8), .pin4(n74138_4_pin4), .pin5(not_1_out), .pin6(in_10),
    .pin7(nIO31), .pin15(nIO24), .pin14(nIO25), .pin13(nIO26), .pin12(nIO27), .pin11(nIO28), .pin10(nIO29),
    .pin9(nIO30));
  _7432 u_7432_1 (
    .pin1(in_11), .pin2(nIO0), .pin3(nIO0SEL), .pin4(in_11), .pin5(nIO1), .pin6(nIO1SEL), .pin13(in_11),
    .pin12(nIO2), .pin11(nIO2SEL), .pin10(in_11), .pin9(nIO3), .pin8(nIO3SEL));
  _7432 u_7432_2 (
    .pin1(in_11), .pin2(nIO8), .pin3(nIO8SEL), .pin4(in_11), .pin5(nIO9), .pin6(nIO9SEL), .pin13(in_11),
    .pin12(nIO10), .pin11(nIO10SEL), .pin10(in_11), .pin9(nIO11), .pin8(nIO11SEL));
  _7432 u_7432_3 (
    .pin1(in_11), .pin2(nIO16), .pin3(nIO16SEL), .pin4(in_11), .pin5(nIO17), .pin6(nIO17SEL), .pin13(in_11),
    .pin12(nIO18), .pin11(nIO18SEL), .pin10(in_11), .pin9(nIO19), .pin8(nIO19SEL));
  _7432 u_7432_4 (
    .pin1(in_11), .pin2(nIO24), .pin3(nIO24SEL), .pin4(in_11), .pin5(nIO25), .pin6(nIO25SEL), .pin13(in_11),
    .pin12(nIO26), .pin11(nIO26SEL), .pin10(in_11), .pin9(nIO27), .pin8(nIO27SEL));
  _7432 u_7432_5 (
    .pin1(in_11), .pin2(nIO4), .pin3(nIO4SEL), .pin4(in_11), .pin5(nIO5), .pin6(nIO5SEL), .pin13(in_11),
    .pin12(nIO6), .pin11(nIO6SEL), .pin10(in_11), .pin9(nIO7), .pin8(nIO7SEL));
  _7432 u_7432_6 (
    .pin1(in_11), .pin2(nIO12), .pin3(nIO12SEL), .pin4(in_11), .pin5(nIO13), .pin6(nIO13SEL), .pin13(in_11),
    .pin12(nIO14), .pin11(nIO14SEL), .pin10(in_11), .pin9(nIO15), .pin8(nIO15SEL));
  _7432 u_7432_7 (
    .pin1(in_11), .pin2(nIO20), .pin3(nIO20SEL), .pin4(in_11), .pin5(nIO21), .pin6(nIO21SEL), .pin13(in_11),
    .pin12(nIO22), .pin11(nIO22SEL), .pin10(in_11), .pin9(nIO23), .pin8(nIO23SEL));
  _7432 u_7432_8 (
    .pin1(in_11), .pin2(nIO28), .pin3(nIO28SEL), .pin4(in_11), .pin5(nIO29), .pin6(nIO29SEL), .pin13(in_11),
    .pin12(nIO30), .pin11(nIO30SEL), .pin10(in_11), .pin9(nIO31), .pin8(nIO31SEL));
  // also tied to GND on the sheet: {n74138_1_pin4, n74138_2_pin4, n74138_3_pin4, n74138_4_pin4}

  // Other names for the same wires on the sheet: A0 = in_1; A1 = in_2; A2 = in_3; A3 = in_4; A4 = in_5; A5 = in_6;
  //   A6 = in_7; A7 = in_8; A8 = in_9; A9 = in_10; nIOSEL = in_11

  // Notes on the sheet:
  //   Typical propagation delay: 13ns (inverter) + 34ns (decoder) + 13ns (OR) = 60ns
endmodule
