// Logisim project pg09_addr_decode_stage1.circ as structural Verilog: 1 circuit, main circuit main
module main (
  input  in_1,
  input  in_2,
  input  in_3,
  input  in_4,
  input  in_5,
  input  in_6,
  input  in_7,
  input  in_8,
  input  in_9,
  input  in_10,
  input  in_11,
  input  in_12,
  input  in_13,
  input  in_14,
  input  in_15,
  input  in_16
);

  wire n74138_1_pin3, nand_1_out, nBRAMSEL, nBROMSEL, nFRAMSEL, nFROMSEL, nIOSEL, nU0;

  _74138 u_74138_1 (
    .pin1(in_14), .pin2(in_15), .pin3(n74138_1_pin3), .pin4(n74138_1_pin3), .pin5(n74138_1_pin3),
    .pin6(in_16), .pin15(nU0), .pin14(nBRAMSEL), .pin13(nBROMSEL), .pin12(nFROMSEL));  // open: pin7, pin11, pin10, pin9
  _74138 u_74138_2 (
    .pin1(in_11), .pin2(in_12), .pin3(in_13), .pin4(in_14), .pin5(in_15), .pin6(in_16), .pin7(nIOSEL));  // open: pin15, pin14, pin13, pin12, pin11, pin10, pin9
  nand nand_1 (nand_1_out, nU0, nU0);
  nand nand_2 (nFRAMSEL, nand_1_out, nIOSEL);
  // also tied to GND on the sheet: n74138_1_pin3

  // Other names for the same wires on the sheet: A0 = in_1; A1 = in_2; A2 = in_3; A3 = in_4; A4 = in_5; A5 = in_6;
  //   A6 = in_7; A7 = in_8; A8 = in_9; A9 = in_10; A10 = in_11; A11 = in_12; A12 = in_13; A13 = in_14; A14 = in_15;
  //   A15 = in_16

  // Notes on the sheet:
  //   Decode upper 32K into /U0, /HBRAM, /BROMSEL, /FROMSEL
  //   Decode /U0 into /IO
  //   Derive /FRAMSEL from /U0 and /IO
endmodule
