// Logisim project pg09_clock_generator.circ as structural Verilog: 1 circuit, main circuit main
module main (
);

  wire a, b, c, CLOCKS_p7, d, E, j_k_ff_2_qn, n74163_1_pin1, not_1_out, not_2_out, Q;

  Clock clock_1 (.out(a));
  // Digital_Oscilloscope #(.nState(30)) CLOCKS: pin names not known; wires that end beside it: b, c, E, Q, a, d, CLOCKS_p7
  _74163 u_74163_1 (
    .pin1(n74163_1_pin1), .pin2(a), .pin3(CLOCKS_p7), .pin4(CLOCKS_p7), .pin5(CLOCKS_p7), .pin6(CLOCKS_p7),
    .pin7(n74163_1_pin1), .pin14(b), .pin13(c), .pin12(d), .pin10(n74163_1_pin1), .pin9(n74163_1_pin1));  // open: pin15, pin11
  J_K_Flip_Flop j_k_ff_1 (.J(j_k_ff_2_qn), .K(not_1_out), .clk(d), .Q(Q));  // open: Qn, preset, reset
  not not_1 (not_1_out, j_k_ff_2_qn);
  J_K_Flip_Flop j_k_ff_2 (.J(Q), .K(not_2_out), .clk(d), .Q(E), .Qn(j_k_ff_2_qn));  // open: preset, reset
  not not_2 (not_2_out, Q);
  // also tied to GND on the sheet: CLOCKS_p7
  // also tied to VCC on the sheet: n74163_1_pin1
endmodule
