// Logisim project pg09_from_brom_decode.circ as structural Verilog: 1 circuit, main circuit main
module main (
  input  in_1,
  input  in_2,
  input  in_3,
  input  in_4,
  input  in_5,
  input  in_6,
  input  in_7,
  input  in_8
);

  wire and_1_out, and_2_out, and_3_out, and_4_out, and_5_out, and_6_out, and_7_out;

  and and_1 (and_1_out, in_1, in_2);
  and and_2 (and_2_out, in_3, in_2);
  and and_3 (and_3_out, in_5, in_2);
  and and_4 (and_4_out, in_6, in_2);
  and and_5 (and_5_out, in_7, in_2);
  and and_6 (and_6_out, in_8, in_2);
  and and_7 (and_7_out, in_2, in_4);
  LED led_1 (.in(and_1_out));
  LED led_2 (.in(and_2_out));
  LED led_3 (.in(and_3_out));
  LED led_4 (.in(and_4_out));
  LED led_5 (.in(and_5_out));
  LED led_6 (.in(and_6_out));
  LED led_7 (.in(and_7_out));

  // Other names for the same wires on the sheet: nBROMSEL = in_4; nFROMSEL = in_2; RB0 = in_1; RB1 = in_3; RB2 = in_5;
  //   RB3 = in_6; RB4 = in_7; RB5 = in_8

  // Notes on the sheet:
  //   Bank number bits
  //   Flash ROM select
endmodule
