// Logisim project pg09_intc.circ as structural Verilog: 1 circuit, main circuit main
module main (
  input  in_1,
  input  in_2,
  input  in_3,
  input  in_4,
  input  in_5,
  input  in_6,
  input  in_7,
  input  in_8,
  input  in_9,
  input  in_10,
  input  in_11,
  input  in_12,
  input  in_13,
  input  in_14,
  input  in_15,
  input  in_16,
  input  in_17,
  input  in_18,
  input  in_19,
  input  in_20,
  input  in_21,
  input  in_22,
  input  in_23,
  input  in_24,
  input  in_25,
  input  in_26,
  input  in_27,
  input  in_28,
  input  in_29,
  input  in_30,
  input  in_31,
  input  in_32,
  input  in_33,
  input  in_34,
  input  in_35,
  input  in_36,
  input  in_37,
  input  in_38,
  input  in_39,
  input  in_40,
  input  in_41,
  input  in_42,
  input  in_43,
  input  in_44,
  input  in_45
);

  wire A0, A1, A1out, A2, A2out, A3, A3out, A4, A5, A6, A7, A8, A9, A10, A11, A12, A13, A14, A15, and_5_out,
       and_6_out, and_11_out, and_12_out, and_17_out, and_18_out, and_19_out, and_20_out, and_21_out,
       and_22_out, and_27_out, and_28_out, and_29_out, CP_LSB, CP_MSB, I0, I1, I2, I3, I4, I5, I6, I7, I8,
       I9, I10, I11, I12, I13, I14, I15, INT0, INT1, INT2, INT3, INT4, INT5, INT6, INT7, INT8, INT9, INT10,
       INT11, INT12, INT13, INT14, INT15, IRQ, IVV, L0, L1, L2, LA, n74138_1_pin3, n74138_1_pin5,
       n74138_1_pin6, n74245_1_pin1, n74245_2_pin1, n74377_1_pin1, n74377_2_pin1, n74377_2_pin3,
       n74377_2_pin4, n74377_2_pin7, n74377_2_pin8, n74377_2_pin13, nA0IN, nIRQ, nUA, or_2_out, U0, U1, U2,
       UA, xA1, xA2, xA3, xA4, xA5, xA6, xA7, xA8, xA9, xA10, xA11, xA12, xA13, xA14, xA15;

  not not_1 (I0, in_4);
  not not_2 (I4, in_28);
  not not_3 (I8, in_5);
  not not_4 (I12, in_29);
  and and_1 (INT0, in_2, I0);
  and and_2 (INT4, in_26, I4);
  and and_3 (INT8, in_3, I8);
  and and_4 (INT12, in_27, I12);
  not not_5 (nA0IN, in_12);
  not not_6 (nUA, UA);
  or or_1 (IRQ, UA, LA);
  not not_7 (nIRQ, IRQ);
  and and_5 (and_5_out, nA0IN, in_6);
  and and_6 (and_6_out, IVV, in_6);
  D_Flip_Flop d_ff_1 (.D(UA), .clk(in_6), .Q(xA4));  // open: Qn, preset, reset
  D_Flip_Flop d_ff_2 (.D(A3out), .clk(in_6), .Q(xA3));  // open: Qn, preset, reset
  D_Flip_Flop d_ff_3 (.D(A2out), .clk(in_6), .Q(xA2));  // open: Qn, preset, reset
  D_Flip_Flop d_ff_4 (.D(A1out), .clk(in_6), .Q(xA1));  // open: Qn, preset, reset
  Priority_Encoder priority_encoder_1 (
    .in0(INT0), .in1(INT1), .in2(INT2), .in3(INT3), .in4(INT4), .in5(INT5), .in6(INT6), .in7(INT7),
    .out({L2, L1, L0}), .en_in(1'b1), .gs(LA));  // open: en_out
  Priority_Encoder priority_encoder_2 (
    .in0(INT8), .in1(INT9), .in2(INT10), .in3(INT11), .in4(INT12), .in5(INT13), .in6(INT14), .in7(INT15),
    .out({U2, U1, U0}), .en_in(1'b1), .gs(UA));  // open: en_out
  _74245 u_74245_1 (
    .pin1(n74245_1_pin1), .pin2(in_12), .pin3(xA1), .pin4(xA2), .pin5(xA3), .pin6(xA4), .pin7(xA5),
    .pin8(xA6), .pin9(xA7), .pin19(in_18), .pin18(A0), .pin17(A1), .pin16(A2), .pin15(A3), .pin14(A4),
    .pin13(A5), .pin12(A6), .pin11(A7));
  Hex_Digit_Display hex_digit_display_1 (.value({xA15, xA14, xA13, xA12}));  // open: dp
  Hex_Digit_Display hex_digit_display_2 (.value({xA11, xA10, xA9, xA8}));  // open: dp
  not not_8 (I1, in_10);
  not not_9 (I5, in_34);
  not not_10 (I9, in_11);
  not not_11 (I13, in_35);
  and and_7 (INT1, in_8, I1);
  and and_8 (INT5, in_32, I5);
  and and_9 (INT9, in_9, I9);
  and and_10 (INT13, in_33, I13);
  Pull_Resistor pull_resistor_1 (.node(L2));
  Pull_Resistor pull_resistor_2 (.node(U2));
  and and_11 (and_11_out, LA, and_5_out);
  and and_12 (and_12_out, UA, and_5_out);
  Hex_Digit_Display hex_digit_display_3 (.value({xA7, xA6, xA5, 1'b0}));  // open: dp
  Pull_Resistor pull_resistor_3 (.node(L1));
  Pull_Resistor pull_resistor_4 (.node(U1));
  or or_2 (or_2_out, and_11_out, and_12_out);
  Hex_Digit_Display hex_digit_display_4 (.value(4'b0000));  // open: dp
  not not_12 (I2, in_16);
  not not_13 (I6, in_39);
  not not_14 (I10, in_17);
  not not_15 (I14, in_40);
  Pull_Resistor pull_resistor_5 (.node(L0));
  Pull_Resistor pull_resistor_6 (.node(U0));
  or or_3 (IVV, or_2_out, and_6_out);
  _74377 u_74377_1 (
    .pin1(n74377_1_pin1), .pin2(xA8), .pin3(in_1), .pin4(in_7), .pin5(xA9), .pin6(xA10), .pin7(in_13),
    .pin8(in_19), .pin9(xA11), .pin19(xA15), .pin18(in_41), .pin17(in_36), .pin16(xA14), .pin15(xA13),
    .pin14(in_31), .pin13(in_25), .pin12(xA12), .pin11(CP_MSB));
  _74245 u_74245_2 (
    .pin1(n74245_2_pin1), .pin2(xA8), .pin3(xA9), .pin4(xA10), .pin5(xA11), .pin6(xA12), .pin7(xA13),
    .pin8(xA14), .pin9(xA15), .pin19(in_18), .pin18(A8), .pin17(A9), .pin16(A10), .pin15(A11), .pin14(A12),
    .pin13(A13), .pin12(A14), .pin11(A15));
  and and_13 (INT2, in_14, I2);
  and and_14 (INT6, in_37, I6);
  and and_15 (INT10, in_15, I10);
  and and_16 (INT14, in_38, I14);
  LED led_1 (.in(nIRQ));
  LED led_2 (.in(IVV));
  not not_16 (I3, in_22);
  not not_17 (I7, in_44);
  not not_18 (I11, in_23);
  not not_19 (I15, in_45);
  and and_17 (and_17_out, LA, L2);
  and and_18 (and_18_out, UA, U2);
  and and_19 (and_19_out, LA, L1);
  and and_20 (and_20_out, UA, U1);
  and and_21 (and_21_out, LA, L0);
  and and_22 (and_22_out, UA, U0);
  Hex_Digit_Display hex_digit_display_5 (.value({A15, A14, A13, A12}));  // open: dp
  Hex_Digit_Display hex_digit_display_6 (.value({A11, A10, A9, A8}));  // open: dp
  and and_23 (INT3, in_20, I3);
  and and_24 (INT7, in_42, I7);
  and and_25 (INT11, in_21, I11);
  and and_26 (INT15, in_43, I15);
  and and_27 (and_27_out, nUA, and_17_out);
  and and_28 (and_28_out, nUA, and_19_out);
  and and_29 (and_29_out, nUA, and_21_out);
  _74377 u_74377_2 (
    .pin1(n74377_2_pin1), .pin3(n74377_2_pin3), .pin4(n74377_2_pin4), .pin7(n74377_2_pin7),
    .pin8(n74377_2_pin8), .pin19(xA7), .pin18(in_41), .pin17(in_36), .pin16(xA6), .pin15(xA5), .pin14(in_31),
    .pin13(n74377_2_pin13), .pin11(CP_LSB));  // open: pin2, pin5, pin6, pin9, pin12
  Hex_Digit_Display hex_digit_display_7 (.value({A7, A6, A5, A4}));  // open: dp
  Hex_Digit_Display hex_digit_display_8 (.value({A3, A2, A1, A0}));  // open: dp
  or or_4 (A3out, and_27_out, and_18_out);
  or or_5 (A2out, and_28_out, and_20_out);
  or or_6 (A1out, and_29_out, and_22_out);
  _74138 u_74138_1 (
    .pin1(in_12), .pin2(in_24), .pin3(n74138_1_pin3), .pin4(in_30), .pin5(n74138_1_pin5),
    .pin6(n74138_1_pin6), .pin15(CP_MSB), .pin14(CP_LSB));  // open: pin7, pin13, pin12, pin11, pin10, pin9
  // also tied to GND on the sheet: {n74377_1_pin1, n74377_2_pin1, n74377_2_pin3, n74377_2_pin4, n74377_2_pin7, n74377_2_pin8, n74377_2_pin13, n74138_1_pin3, n74138_1_pin5}
  // also tied to VCC on the sheet: {n74245_1_pin1, n74245_2_pin1, n74138_1_pin6}

  // Other names for the same wires on the sheet: BS = in_6; D0 = in_1; D1 = in_7; D2 = in_13; D3 = in_19; D4 = in_25;
  //   D5 = in_31; D6 = in_36; D7 = in_41; E0 = in_2; E1 = in_8; E2 = in_14; E3 = in_20; E4 = in_26; E5 = in_32;
  //   E6 = in_37; E7 = in_42; E8 = in_3; E9 = in_9; E10 = in_15; E11 = in_21; E12 = in_27; E13 = in_33; E14 = in_38;
  //   E15 = in_43; nCS = in_30; nI0 = in_4; nI1 = in_10; nI2 = in_16; nI3 = in_22; nI4 = in_28; nI5 = in_34;
  //   nI6 = in_39; nI7 = in_44; nI8 = in_5; nI9 = in_11; nI10 = in_17; nI11 = in_23; nI12 = in_29; nI13 = in_35;
  //   nI14 = in_40; nI15 = in_45; nOE = in_18; nWR = in_24; A0IN = in_12; xA0 = in_12

  // Notes on the sheet:
  //   table offset.
  //   Priority-encode INT0-INT7.
  //   Priority-encode INT8-INT15.
  //   Inverted copies of active-low IRQ inputs.
  //   Mix with active-high IRQ enable inputs.
  //   Multiplex to and convert highest priority interrupt into an interrupt vector
  //   Latch the vector table offset when the IRQ vector fetch begins.
  //   Tri-state output buffers
  //   Vector Base Register
  //   VBR (MSB)
  //   Vector Base Register
  //   VBR (LSB)
  //   Vector fetch address
  //   Active-low IRQ output to CPU.
  //   Interrupt Vector Valid signal to ABUSSEL.
  //   Generate write strobe for VBR
endmodule
