// Logisim project pg09_intmux_av.circ as structural Verilog: 1 circuit, main circuit main
module main (
  input  in_1,
  input  in_2,
  input  in_3,
  input  in_4,
  input  in_5,
  input  in_6,
  input  in_7,
  input  in_8,
  input  in_9,
  input  in_10
);

  wire A1, A1out, A2, A2out, A3, A3out, A4, and_1_out, and_2_out, and_3_out, and_4_out, and_5_out, and_6_out,
       and_7_out, and_8_out, and_9_out, and_10_out, and_11_out, and_12_out, and_13_out, IRQ, IVV, nA0IN,
       nIRQ, nUA, or_2_out;

  not not_1 (nA0IN, in_10);
  not not_2 (nUA, in_2);
  or or_1 (IRQ, in_2, in_6);
  not not_3 (nIRQ, IRQ);
  and and_1 (and_1_out, nA0IN, in_1);
  and and_2 (and_2_out, IVV, in_1);
  D_Flip_Flop d_ff_1 (.D(in_2), .clk(in_1), .Q(A4));  // open: Qn, preset, reset
  D_Flip_Flop d_ff_2 (.D(A3out), .clk(in_1), .Q(A3));  // open: Qn, preset, reset
  D_Flip_Flop d_ff_3 (.D(A2out), .clk(in_1), .Q(A2));  // open: Qn, preset, reset
  D_Flip_Flop d_ff_4 (.D(A1out), .clk(in_1), .Q(A1));  // open: Qn, preset, reset
  and and_3 (and_3_out, in_6, and_1_out);
  and and_4 (and_4_out, in_2, and_1_out);
  or or_2 (or_2_out, and_3_out, and_4_out);
  or or_3 (IVV, or_2_out, and_2_out);
  LED led_1 (.in(nIRQ));
  LED led_2 (.in(IVV));
  LED led_3 (.in(A4));
  LED led_4 (.in(A3));
  LED led_5 (.in(A2));
  LED led_6 (.in(A1));
  LED led_7 (.in(in_10));
  and and_5 (and_5_out, in_6, in_7);
  and and_6 (and_6_out, in_2, in_3);
  and and_7 (and_7_out, in_6, in_8);
  and and_8 (and_8_out, in_2, in_4);
  and and_9 (and_9_out, in_6, in_9);
  and and_10 (and_10_out, in_2, in_5);
  and and_11 (and_11_out, nUA, and_5_out);
  and and_12 (and_12_out, nUA, and_7_out);
  and and_13 (and_13_out, nUA, and_9_out);
  or or_4 (A3out, and_11_out, and_6_out);
  or or_5 (A2out, and_12_out, and_8_out);
  or or_6 (A1out, and_13_out, and_10_out);

  // Other names for the same wires on the sheet: A0 = in_10; A0IN = in_10; BS = in_1; L0 = in_9; L1 = in_8; L2 = in_7;
  //   LA = in_6; U0 = in_5; U1 = in_4; U2 = in_3; UA = in_2

  // Notes on the sheet:
  //   (nOE input not shown.)
  //   input is asserted.
  //   Active-low IRQ output to CPU.
  //   Interrupt Vector Valid output to ABUSSEL.
  //   A0-A4 drive the address bus when the nOE
endmodule
