// Logisim project pg09_lbram_decode.circ as structural Verilog: 1 circuit, main circuit main
module main (
  input  in_1,
  input  in_2,
  input  in_3,
  input  in_4,
  input  in_5,
  input  in_6,
  input  in_7,
  input  in_8,
  input  in_9,
  input  in_10,
  input  in_11,
  input  in_12,
  input  in_13,
  input  in_14
);

  wire LRBS0, LRBS1, LRBS2, LRBS3, LRCS0, LRCS1, n74157_1_pin15, n74157_2_pin10, n74157_2_pin11,
       n74157_2_pin13, n74157_2_pin14, n74157_2_pin15, nCHIP0, nCHIP1, nCHIP2, nCHIP3;

  _74157 u_74157_1 (
    .pin1(in_1), .pin2(in_2), .pin3(in_3), .pin4(LRBS0), .pin5(in_5), .pin6(in_6), .pin7(LRBS1),
    .pin15(n74157_1_pin15), .pin14(in_9), .pin13(in_10), .pin12(LRBS3), .pin11(in_7), .pin10(in_8),
    .pin9(LRBS2));
  _74157 u_74157_2 (
    .pin1(in_1), .pin2(in_11), .pin3(in_12), .pin4(LRCS0), .pin5(in_13), .pin6(in_14), .pin7(LRCS1),
    .pin15(n74157_2_pin15), .pin14(n74157_2_pin14), .pin13(n74157_2_pin13), .pin11(n74157_2_pin11),
    .pin10(n74157_2_pin10));  // open: pin12, pin9
  Hex_Digit_Display hex_digit_display_1 (.value({LRBS3, LRBS2, LRBS1, LRBS0}));  // open: dp
  LED led_1 (.in(nCHIP0));
  LED led_2 (.in(nCHIP1));
  LED led_3 (.in(nCHIP2));
  LED led_4 (.in(nCHIP3));
  _74139 u_74139_1 (
    .pin1(in_4), .pin2(LRCS0), .pin3(LRCS1), .pin4(nCHIP0), .pin5(nCHIP1), .pin6(nCHIP2), .pin7(nCHIP3));  // open: pin15, pin14, pin13, pin12, pin11, pin10, pin9
  // also tied to GND on the sheet: {n74157_1_pin15, n74157_2_pin15, n74157_2_pin14, n74157_2_pin13, n74157_2_pin11, n74157_2_pin10}

  // Other names for the same wires on the sheet: A14 = in_1; A15 = in_4; LR0B0 = in_2; LR0B1 = in_5; LR0B2 = in_7;
  //   LR0B3 = in_9; LR0B4 = in_11; LR0B5 = in_13; LR1B0 = in_3; LR1B1 = in_6; LR1B2 = in_8; LR1B3 = in_10;
  //   LR1B4 = in_12; LR1B5 = in_14

  // Notes on the sheet:
  //   Bank number
  //   Chip select outputs are active-low.
endmodule
