// Logisim project pg09_psu_iosel.circ as structural Verilog: 1 circuit, main circuit main
module main (
  input  in_1,
  input  in_2,
  input  in_3,
  input  in_4,
  input  in_5,
  input  in_6,
  input  in_7
);

  wire nPSUWR;

  _74138 u_74138_1 (
    .pin1(in_1), .pin2(in_5), .pin3(in_3), .pin4(in_2), .pin5(in_4), .pin6(in_7), .pin11(nPSUWR));  // open: pin7, pin15, pin14, pin13, pin12, pin10, pin9

  // Other names for the same wires on the sheet: A0 = in_3; A1 = in_4; A2 = in_5; A3 = in_6; A4 = in_7;
  //   nIO0SEL = in_2; nWR = in_1
endmodule
